// Logisim project 6651071085_LAB1_Bai6.5.circ as structural Verilog: 1 circuit, main circuit main
module main (
  input  A,
  input  B,
  input  A_B,
  input  A_B_2,
  input  A_B_3,
  output A_B_4,
  output A_B_5,
  output A_B_6
);

  wire and_1_out, and_3_out, not_1_out, not_2_out, xnor_1_out;

  not not_1 (not_1_out, A);
  not not_2 (not_2_out, B);
  xnor xnor_1 (xnor_1_out, A, B);
  and and_1 (and_1_out, A, A_B, not_2_out);
  and and_2 (A_B_4, xnor_1_out, A_B);
  and and_3 (and_3_out, A_B, not_1_out, B);
  or or_1 (A_B_5, and_1_out, A_B_2);
  or or_2 (A_B_6, and_3_out, A_B_3);

  // Notes on the sheet:
  //   Phạm Thanh Trúc _ 6651071085 
endmodule
