// Logisim project 6651071085_LAB1_Bai6.6.circ as structural Verilog: 1 circuit, main circuit main
module main (
  input  Reset,
  output [3:0] Q_3_0
);

  wire clock_1_out, N0, N1, N2, N3;

  Clock clock_1 (.out(clock_1_out));
  D_Flip_Flop FF0 (.clk(clock_1_out), .D(N0), .Q(Q_3_0[0]), .Qn(N0), .en(1'b1), .reset(Reset));  // open: preset
  D_Flip_Flop FF1 (.clk(N0), .D(N1), .Q(Q_3_0[1]), .Qn(N1), .en(1'b1), .reset(Reset));  // open: preset
  D_Flip_Flop FF2 (.clk(N1), .D(N2), .Q(Q_3_0[2]), .Qn(N2), .en(1'b1), .reset(Reset));  // open: preset
  D_Flip_Flop FF3 (.clk(N2), .D(N3), .Q(Q_3_0[3]), .Qn(N3), .en(1'b1), .reset(Reset));  // open: preset

  // Notes on the sheet:
  //   Phạm Thanh Trúc _ 6651071085 
endmodule
