// Logisim project 6651071085_LAB1_Bai6.7.circ as structural Verilog: 1 circuit, main circuit main
module main (
  input  [3:0] Data_in,
  input  [2:0] Addr,
  input  Load,
  output [3:0] Data_out
);

  wire clock_1_out, not_1_out;

  Clock clock_1 (.out(clock_1_out));
  not not_1 (not_1_out, Load);
  RAM #(.addrWidth(3), .dataWidth(4)) ram_1 (
    .addr(Addr), .data(Data_out), .sel(1'b1), .clk(clock_1_out), .ld(not_1_out));  // open: clr
  assign Data_out = Load ? Data_in : 4'bz;  // Controlled_Buffer controlled_buffer_1

  // Notes on the sheet:
  //   Phạm Thanh Trúc _ 6651071085 
endmodule
